# Fritzing sketch RangeSensorBBProto (saved by Fritzing 0.9.2b)
circuit board: 2.0378cm x 3.32994cm
breadboards: 1

parts:
  Attiny85 = attiny85 [package=dip]
  LED = LED - 3mm [color="Green (555nm)" current=20mA package="3 mm [THT]"]
  10uF = Electrolytic Capacitor [capacitance=10µF voltage=10V package="100 mil [THT, electrolytic]"]
  3K9 = Resistor [tolerance=±5% resistance=3.9k package=THT]
  180R = Resistor [tolerance=±5% resistance=180 package=THT]
  Max_Range = Trimmer Potentiometer [maximum_resistance=10kΩ package=THT]
  S1 = SPST Switch [package=switch-spdt_lock.007s]
  F_Out_Bit = female pin header, 3 pins [form="♀ (female)"]
  Sensor = Parallax Ping))) Ultrasonic Range Sendor [part_number=28014]
  IN_M_Bit = female pin header, 3 pins [form="♀ (female)"]

nets:
  N1: Attiny85.Pin_2, Sensor.Sig
  N2: Attiny85.Pin_3, Max_Range.wiper
  N3: Attiny85.Pin_4, LED.cathode, 10uF.-, Max_Range.leg1, S1.S, F_Out_Bit.pin3, Sensor.GND, IN_M_Bit.pin3
  N4: Attiny85.Pin_5, 180R.Pin_1, S1.P
  N5: Attiny85.Pin_6, 3K9.Pin_1
  N6: Attiny85.Pin_8, Max_Range.leg2, S1.O, F_Out_Bit.pin1, Sensor.5V, IN_M_Bit.pin1
  N7: LED.anode, 180R.Pin_0
  N8: 10uF.+, 3K9.Pin_0, F_Out_Bit.pin2

notes:
  bitsnap F
  out to next bit
  bitsnap M in from previous bit
  Close
  Far
  Max
  LittleBits Range
  KidElectron & Perednik
  V0.7
  Sensor
  SPDT
  +
  --
  sig
  M
  -->
  F
  LittleBits Ultrasonic Range Sensor, A range rensor for the LittleBits system, .5
  -

// code stored in the sketch: RangeSensor.ino
/* Ping))) Sensor

   This sketch reads a PING))) ultrasonic rangefinder and returns the
   distance to the closest object in range. To do this, it sends a pulse
   to the sensor to initiate a reading, then listens for a pulse
   to return.  The length of the returning pulse is proportional to
   the distance of the object from the sensor.

   The circuit:
  * +V connection of the PING))) attached to +5V
  * GND connection of the PING))) attached to ground
  * SIG connection of the PING))) attached to digital pin 2

   http://www.arduino.cc/en/Tutorial/Ping

   created 3 Nov 2008
   by David A. Mellis
   modified 06 Aug 2011
   by Tom Igoe
   modified 22 Jun 2015
   by Shai Perednik shaiss@gmail.com

   This example code is in the public domain.

 */

// this constant won't change.  It's the pin number
// of the sensor's output:
const int trimpot = A2;
const int slidebtn = 0;
const int pingPin = 3; //Sig pin of the Ping))) Sensor
const int ledPin = 1; //The pin the LED is attached to
const int ledRangeMode = 2; //built in LED

//define some vars
float brightness = 0; //set the initial value to null
int analogVolts = 0; //set initial value to null for voltage out
float trimpotval = 0; //potentiometer on trimpot pin's current position
float maxrange = 0; //max range sensor is set to

void setup() {
  // initialize serial communication:
  //Serial.begin(9600);
  pinMode(ledPin, OUTPUT);  //declare ledPin as an output
  pinMode(slidebtn, INPUT); //declare the slidebtn as an input
  pinMode(ledRangeMode, OUTPUT); //indicate the slidebtn mode, close or far


}

void loop()
{
  //read trimpot's value
  trimpotval = analogRead(trimpot);

  maxrange = (trimpotval/1023)*300;
  
  // establish variables for duration of the ping,
  // and the distance result in inches and centimeters:
  long duration, inches, cm;

  // The PING))) is triggered by a HIGH pulse of 2 or more microseconds.
  // Give a short LOW pulse beforehand to ensure a clean HIGH pulse:
  pinMode(pingPin, OUTPUT);
  digitalWrite(pingPin, LOW);
  delayMicroseconds(2);
  digitalWrite(pingPin, HIGH);
  delayMicroseconds(5);
  digitalWrite(pingPin, LOW);

  // The same pin is used to read the signal from the PING))): a HIGH  
  // pulse whose duration is the time (in microseconds) from the sending
  // of the ping to the reception of its echo off of an object.
  pinMode(pingPin, INPUT);
  duration = pulseIn(pingPin, HIGH);

  // convert the time into a distance
 // inches = microsecondsToInches(duration);
  cm = microsecondsToCentimeters(duration);

  //convert distance of object to brightness.  
  //Ping))) range is 2cm - 3M/.78in - 118.11in
  if (digitalRead(slidebtn) == HIGH) {
    //if slide btn is HIGH or on, then sensor is in close mode
    brightness = ((((cm/maxrange)*255)-255)*-1);  //closer == brighter/higher voltage.  If cm =0 returns 255.
    digitalWrite(ledRangeMode, HIGH);//rangemode LED on
  }
  else {
    //if slide btn is LOW or off, then sensor is in far mode
    brightness = ((cm/maxrange))*255; //farther == brighter/higher voltage.  If cm = 300 returns 255
    digitalWrite(ledRangeMode, LOW); //rangemode LED off
  }

  if (brightness > 255){brightness = 255;}
  if (brightness < 0) {brightness = 0;}
    
  //Serial.println(brightness);
  
  //write distance to LED //same pin used as output pin to RC Lowpass Filter, then to Littlebits SIG OUT
  analogWrite(ledPin, brightness);

  delay(100);
}

long microsecondsToInches(long microseconds)
{
  // According to Parallax's datasheet for the PING))), there are
  // 73.746 microseconds per inch (i.e. sound travels at 1130 feet per
  // second).  This gives the distance travelled by the ping, outbound
  // and return, so we divide by 2 to get the distance of the obstacle.
  // See: http://www.parallax.com/dl/docs/prod/acc/28015-PING-v1.3.pdf
  return microseconds / 74 / 2;
}

long microsecondsToCentimeters(long microseconds)
{
  // The speed of sound is 340 m/s or 29 microseconds per centimeter.
  // The ping travels out and back, so to find the distance of the
  // object we take half of the distance travelled.
  return microseconds / 29 / 2;
}

// code stored in the sketch: RangeSensorWLCD.ino
/* Ping))) Sensor

   This sketch reads a PING))) ultrasonic rangefinder and returns the
   distance to the closest object in range. To do this, it sends a pulse
   to the sensor to initiate a reading, then listens for a pulse
   to return.  The length of the returning pulse is proportional to
   the distance of the object from the sensor.

   The circuit:
	* +V connection of the PING))) attached to +5V
	* GND connection of the PING))) attached to ground
	* SIG connection of the PING))) attached to digital pin 2

   http://www.arduino.cc/en/Tutorial/Ping

   created 3 Nov 2008
   by David A. Mellis
   modified 06 Aug 2011
   by Tom Igoe
	 modified 22 Jun 2015
   by Shai Perednik shaiss@gmail.com

   This example code is in the public domain.

 */

#include <TFT.h>  // Arduino LCD library
#include <SPI.h>

// this constant won't change.  It's the pin number
// of the sensor's output:
const int pingPin = 2;

// pin definition for the Uno
#define cs   10
#define dc   9
#define rst  8

// create an instance of the library
TFT TFTscreen = TFT(cs, dc, rst);

// char array to print to the screen
char sensorPrintout[6];

void setup() {
  // initialize serial communication:
  Serial.begin(9600);
  
    // Put this line at the beginning of every sketch that uses the GLCD:
  TFTscreen.begin();

  // clear the screen with a black background
  TFTscreen.background(0, 0, 0);

  // write the static text to the screen
  // set the font color to white
  TFTscreen.stroke(255, 255, 255);
  // set the font size
  TFTscreen.setTextSize(2);
  // write the text to the top left corner of the screen
  TFTscreen.text("Sensor Value :\n ", 0, 0);
  // ste the font size very large for the loop
  TFTscreen.setTextSize(5);
  TFTscreen.text("in", 0, 60);
}

void loop()
{
  // establish variables for duration of the ping,
  // and the distance result in inches and centimeters:
  long duration, inches, cm;

  // The PING))) is triggered by a HIGH pulse of 2 or more microseconds.
  // Give a short LOW pulse beforehand to ensure a clean HIGH pulse:
  pinMode(pingPin, OUTPUT);
  digitalWrite(pingPin, LOW);
  delayMicroseconds(2);
  digitalWrite(pingPin, HIGH);
  delayMicroseconds(5);
  digitalWrite(pingPin, LOW);

  // The same pin is used to read the signal from the PING))): a HIGH  
  // pulse whose duration is the time (in microseconds) from the sending
  // of the ping to the reception of its echo off of an object.
  pinMode(pingPin, INPUT);
  duration = pulseIn(pingPin, HIGH);

  // convert the time into a distance
  inches = microsecondsToInches(duration);
  cm = microsecondsToCentimeters(duration);

  Serial.print(inches);
  Serial.print("in, ");
  Serial.print(cm);
  Serial.print("cm");
  Serial.println();

  String sensorVal = String(inches);
  //sensorVal += " in";
  sensorVal.toCharArray(sensorPrintout, 6);
  
  
  // set the font color
  TFTscreen.stroke(255, 255, 255);
  // print the sensor value
  TFTscreen.text(sensorPrintout, 0, 20);
  // wait for a moment
  delay(100);
  // erase the text you just wrote
  TFTscreen.stroke(0, 0, 0);
  TFTscreen.text(sensorPrintout, 0, 20);
}

long microsecondsToInches(long microseconds)
{
  // According to Parallax's datasheet for the PING))), there are
  // 73.746 microseconds per inch (i.e. sound travels at 1130 feet per
  // second).  This gives the distance travelled by the ping, outbound
  // and return, so we divide by 2 to get the distance of the obstacle.
  // See: http://www.parallax.com/dl/docs/prod/acc/28015-PING-v1.3.pdf
  return microseconds / 74 / 2;
}

long microsecondsToCentimeters(long microseconds)
{
  // The speed of sound is 340 m/s or 29 microseconds per centimeter.
  // The ping travels out and back, so to find the distance of the
  // object we take half of the distance travelled.
  return microseconds / 29 / 2;
}
